# Fritzing sketch wand (saved by Fritzing 0.9.3b)

parts:
  U3 = RF-LINK_TX [package=rf-link_tx]
  Part3 = InvenSense MPU6050
  VCC2 = Battery block 9V
  S2 = Pushbutton [package="[SMD]"]
  Part4 = Arduino Nano (Rev3.0)
  LED2 = LEDs [package=led10mm]

nets:
  N1: U3.DATA, Part4.D12/MISO
  GND: U3.GND, Part3.GND, VCC2.-, Part4.GND, LED2.C
  +5V: U3.+5V, Part3.VCC, Part4.5V
  N2: Part3.SCL, Part4.A5
  N3: Part3.SDA, Part4.A4
  N4: S2.Pin_1, S2.Pin_2, Part4.VIN
  N5: Part4.D7, LED2.A

custom parts:
  RF-LINK_TX: Common RF transmitter of the 315.00Mhz varity
