# Fritzing sketch bar (saved by Fritzing 0.9.3b)

parts:
  Part3 = Arduino Uno (Rev3)
  KY-1 = Keyes Relay [package=THT]
  KY-2 = Keyes Relay [package=THT]
  KY-3 = Keyes Relay [package=THT]
  KY-4 = Keyes Relay [package=THT]
  U3 = RF-LINK_RX [package=rf-link_rx]
  Power_plug1 = Power plug
  Power_plug2 = Power plug
  Power_plug3 = Power plug
  Power_plug4 = Power plug

nets:
  N1: Part3.D11_PWM/MOSI, U3.Data
  N2: Part3.D2, KY-4.signal
  N3: Part3.D3_PWM, KY-1.signal
  N4: Part3.D4, KY-2.signal
  N5: Part3.D5_PWM, KY-3.signal
  5V: Part3.5V, KY-1.power, KY-2.power, KY-3.power, KY-4.power, U3.VCC
  GND: Part3.GND, KY-1.ground, KY-2.ground, KY-3.ground, KY-4.ground, U3.GND
  N6: KY-1.NC, Power_plug3.VCC
  N7: KY-1.C, KY-2.C, KY-3.C, KY-4.C
  N8: KY-2.NC, Power_plug2.VCC
  N9: KY-3.NC, Power_plug1.VCC
  N10: KY-4.NC, Power_plug4.VCC
  GND_2: Power_plug1.GND, Power_plug2.GND, Power_plug3.GND, Power_plug4.GND

notes:
  Incoming Live wire
  Common neutral
  AC outlets

custom parts:
  Keyes Relay: The Keyes 5V relay module is suitable for SCM development, home appliance control. It uses a 5V~12V TIL control signal which can control DC / AC signal.
  RF-LINK_RX: RF Link receivers- WRL-8947, 8948, 8949, 8950
